// Logisim project Ch7.circ as structural Verilog
module processor (
);

  wire AluInAClk, AluInBClk, AluOutClk, CarryInClk, Decode, InsRegClk, MemClk, MemInClk, MemOutClk,
       MemSelClk, pull_resistor_1_node, RegClk, RegInClk, RegOutClk, RegSelClk;
  wire [1:0] InsRegSel, RegInpSel, register_1_q;
  wire [2:0] multiplexer_2_out, n16_bit_alu_2_1_out_6, register_1_q_2, register_1_q_3, register_1_q_4,
       register_3_q, register_6_q, register_7_q, register_11_q, register_15_q;
  wire [3:0] control_logic_1_microstep, register_2_q, register_8_q;
  wire [4:0] register_1_q_5;
  wire [4:4] register_2_q_2;
  wire [7:0] register_9_q;
  wire [15:0] addtwonum_1_data_out, carry_in_1_out, multiplexer_1_out, n16_bit_alu_2_1_result, register_4_q,
       register_5_q, register_10_q, register_13_q, register_16_q, register_17_q, register_18_q,
       register_19_q, Registers_data_out, Registers_r0, Registers_r1, Registers_r2, Registers_r3,
       Registers_r4, Registers_r5, Registers_r6, Registers_r7;

  Hex_Digit_Display hex_digit_display_1 (.value(control_logic_1_microstep));  // open: dp
  Control_Logic control_logic_1 (
    .Decode(Decode), .InsRegClk(InsRegClk), .AluInAClk(AluInAClk), .AluInBClk(AluInBClk),
    .AluOutClk(AluOutClk), .RegClk(RegClk), .RegOutClk(RegOutClk), .MemClk(MemClk), .MemSelClk(MemSelClk),
    .MemInClk(MemInClk), .MemOutClk(MemOutClk), .CarryInClk(CarryInClk), .RegInpSel(RegInpSel),
    .InsRegSel(InsRegSel), .OpCode({register_2_q_2[4], register_2_q}), .MicroStep(control_logic_1_microstep),
    .RegSelClk(RegSelClk), .RegInClk(RegInClk));  // open: N_Z_P_2, N_Z_P
  Register #(.width(16), .trigger("high")) register_1 (
    .D(register_19_q), .Q({register_1_q_5, register_1_q_4, register_1_q_3, register_1_q_2, register_1_q}),
    .clk(InsRegClk));  // open: en, clr
  Register #(.width(5), .trigger("high")) register_2 (
    .D(register_1_q_5), .Q({register_2_q_2[4], register_2_q}), .clk(Decode));  // open: en, clr
  Register #(.width(3), .trigger("high")) register_3 (
    .D(register_1_q_4), .Q(register_3_q), .clk(Decode));  // open: en, clr
  Register #(.width(16), .trigger("high")) register_4 (
    .D(register_18_q), .Q(register_4_q), .clk(AluInAClk));  // open: en, clr
  Register #(.width(16), .trigger("high")) register_5 (
    .D(register_18_q), .Q(register_5_q), .clk(AluInBClk));  // open: en, clr
  Register #(.width(3), .trigger("high")) register_6 (
    .D(register_1_q_2), .Q(register_6_q), .clk(Decode));  // open: en, clr
  Register #(.width(3), .trigger("high")) register_7 (
    .D(register_1_q_3), .Q(register_7_q), .clk(Decode));  // open: en, clr
  Register #(.width(4), .trigger("high")) register_8 (
    .D(register_2_q), .Q(register_8_q), .clk(register_2_q_2[4]));  // open: en, clr
  Register #(.trigger("high")) register_9 (
    .D({register_1_q_3, register_1_q_2, register_1_q}), .Q(register_9_q), .clk(Decode));  // open: en, clr
  Register #(.width(16), .trigger("high")) register_10 (
    .D(n16_bit_alu_2_1_result), .Q(register_10_q), .clk(AluOutClk));  // open: en, clr
  _16_bit_alu_2 u_16_bit_alu_2_1 (
    .A(register_4_q), .B(register_5_q), .Result(n16_bit_alu_2_1_result), .in_1(register_8_q),
    .out_6(n16_bit_alu_2_1_out_6));  // open: CarryOut_Overflow
  Register #(.width(3), .trigger("high")) register_11 (
    .D(n16_bit_alu_2_1_out_6), .Q(register_11_q), .clk(register_2_q_2[4]));  // open: en, clr
  Multiplexer #(.select(2), .width(16), .enable("false")) multiplexer_1 (
    .in0({{8{1'b0}}, register_9_q}), .in1(register_19_q), .in2(register_10_q), .in3(carry_in_1_out),
    .out(multiplexer_1_out), .sel(RegInpSel));
  // Probe on RegInpSel
  Carry_In carry_in_1 (.IN(register_18_q), .Out(carry_in_1_out), .Carry_In(CarryInClk));
  Register #(.width(16), .trigger("high")) register_12 (.D(carry_in_1_out), .clk(1'b1));  // open: en, Q, clr
  Pull_Resistor pull_resistor_1 (.node(pull_resistor_1_node));
  Multiplexer #(.select(2), .width(3), .disabled(0)) multiplexer_2 (
    .in0(3'b000), .in1(register_3_q), .in2(register_7_q), .in3(register_6_q), .out(multiplexer_2_out),
    .sel(InsRegSel), .en(RegSelClk));
  // Probe on multiplexer_2_out
  Register #(.width(16), .trigger("high")) register_13 (
    .D(multiplexer_1_out), .Q(register_13_q), .clk(RegInClk));  // open: en, clr
  Register #(.width(16), .trigger("high")) register_14 (.D(register_18_q), .clk(1'b1));  // open: en, Q, clr
  Register #(.width(3), .trigger("high")) register_15 (
    .D(multiplexer_2_out), .Q(register_15_q), .clk(RegSelClk), .clr(pull_resistor_1_node));  // open: en
  _16_bit_8_word_register Registers (
    .Data_In(register_13_q), .Clock(RegClk), .Data_Out(Registers_data_out), .Select_In(register_15_q),
    .R0(Registers_r0), .R1(Registers_r1), .R2(Registers_r2), .R3(Registers_r3), .R4(Registers_r4),
    .R5(Registers_r5), .R6(Registers_r6), .R7(Registers_r7));
  Register #(.width(16), .trigger("high")) register_16 (
    .D(register_18_q), .Q(register_16_q), .clk(MemSelClk));  // open: en, clr
  AddTwoNum addtwonum_1 (
    .Data_In(register_17_q), .Data_Out(addtwonum_1_data_out), .Memory_Address(register_16_q), .Clock(MemClk));  // open: CLEAR
  Register #(.width(16), .trigger("high")) register_17 (
    .D(register_18_q), .Q(register_17_q), .clk(MemInClk));  // open: en, clr
  Register #(.width(16), .trigger("high")) register_18 (
    .D(Registers_data_out), .Q(register_18_q), .clk(RegOutClk));  // open: en, clr
  Register #(.width(16), .trigger("high")) register_19 (
    .D(addtwonum_1_data_out), .Q(register_19_q), .clk(MemOutClk));  // open: en, clr
  Register #(.width(16), .trigger("high")) register_20 (.D(Registers_r0), .clk(1'b1));  // open: en, Q, clr
  Register #(.width(16), .trigger("high")) register_21 (.D(Registers_r1), .clk(1'b1));  // open: en, Q, clr
  Register #(.width(16), .trigger("high")) register_22 (.D(Registers_r2), .clk(1'b1));  // open: en, Q, clr
  Register #(.width(16), .trigger("high")) register_23 (.D(Registers_r3), .clk(1'b1));  // open: en, Q, clr
  Register #(.width(16), .trigger("high")) register_24 (.D(Registers_r4), .clk(1'b1));  // open: en, Q, clr
  Register #(.width(16), .trigger("high")) register_25 (.D(Registers_r5), .clk(1'b1));  // open: en, Q, clr
  Register #(.width(16), .trigger("high")) register_26 (.D(Registers_r6), .clk(1'b1));  // open: en, Q, clr
  Register #(.width(16), .trigger("high")) register_27 (.D(Registers_r7), .clk(1'b1));  // open: en, Q, clr
endmodule

module Control_Logic (
  input  [4:0] OpCode,
  input  [2:0] N_Z_P,
  input  [2:0] N_Z_P_2,
  output [3:0] MicroStep,
  output [1:0] InsRegSel,
  output RegSelClk,
  output RegOutClk,
  output MemOutClk,
  output MemSelClk,
  output CarryInClk,
  output [1:0] RegInpSel,
  output RegInClk,
  output AluInAClk,
  output AluInBClk,
  output AluOutClk,
  output MemInClk,
  output MemClk,
  output RegClk,
  output InsRegClk,
  output Decode
);

  wire and_1_out, and_2_out, and_3_out, and_4_out, and_5_out, and_6_out, clock_1_out, not_1_out, not_2_out,
       not_3_out, or_1_out, or_2_out, or_3_out, or_4_out;
  wire [3:0] demultiplexer_1_out0;
  wire [9:0] demultiplexer_1_out6, demultiplexer_2_out0, demultiplexer_2_out1, demultiplexer_3_out0,
       demultiplexer_3_out1, demultiplexer_3_out2, demultiplexer_3_out3;

  not not_1 (not_1_out, OpCode[4]);
  and and_1 (and_1_out, not_1_out, OpCode[3], OpCode[2]);
  Pull_Resistor pull_resistor_1 (.node(and_1_out));
  not not_2 (not_2_out, and_1_out);
  Clock clock_1 (.out(clock_1_out));
  and and_2 (and_2_out, N_Z_P[2], N_Z_P_2[2]);
  Counter_part #(.width(4), .max('hf)) counter_1 (
    .Q(MicroStep), .clk(and_3_out), .clr(or_1_out));  // open: load, D, count, carry
  and and_3 (and_3_out, clock_1_out, not_2_out);
  or or_1 (or_1_out, and_4_out, demultiplexer_3_out2[5], demultiplexer_3_out1[3], demultiplexer_3_out0[5], demultiplexer_2_out0[9]);
  and and_4 (and_4_out, or_2_out, demultiplexer_3_out3[0]);
  or or_2 (or_2_out, and_2_out, and_5_out, and_6_out);
  and and_5 (and_5_out, N_Z_P[1], N_Z_P_2[1]);
  and and_6 (and_6_out, N_Z_P[0], N_Z_P_2[0]);
  Demultiplexer #(.select(4), .enable("false")) demultiplexer_1 (
    .out0(demultiplexer_1_out0[0]), .out1(demultiplexer_1_out0[1]), .out2(demultiplexer_1_out0[2]),
    .out3(demultiplexer_1_out0[3]), .out4(InsRegClk), .out5(Decode), .out6(demultiplexer_1_out6[0]),
    .out7(demultiplexer_1_out6[1]), .out8(demultiplexer_1_out6[2]), .out9(demultiplexer_1_out6[3]),
    .out10(demultiplexer_1_out6[4]), .out11(demultiplexer_1_out6[5]), .out12(demultiplexer_1_out6[6]),
    .out13(demultiplexer_1_out6[7]), .out14(demultiplexer_1_out6[8]), .out15(demultiplexer_1_out6[9]),
    .in(1'b1), .sel(MicroStep));
  Demultiplexer #(.width(10), .disabled(0), .enable("false")) demultiplexer_2 (
    .out0({demultiplexer_2_out0[9:7], AluOutClk, AluInBClk, demultiplexer_2_out0[4:3], AluInAClk, demultiplexer_2_out0[1:0]}),
    .out1(demultiplexer_2_out1), .in(demultiplexer_1_out6), .sel(not_3_out));
  not not_3 (not_3_out, OpCode[4]);
  Demultiplexer #(.select(2), .width(10), .enable("false")) demultiplexer_3 (
    .out0(demultiplexer_3_out0), .out1(demultiplexer_3_out1),
    .out2({demultiplexer_3_out2[9:4], MemClk, demultiplexer_3_out2[2:0]}), .out3(demultiplexer_3_out3),
    .in(demultiplexer_2_out1), .sel(OpCode[1:0]));
  or or_3 (or_3_out, demultiplexer_2_out0[0], demultiplexer_3_out0[2], demultiplexer_3_out1[0], demultiplexer_3_out2[2]);
  or or_4 (or_4_out, demultiplexer_2_out0[3], demultiplexer_3_out2[0], demultiplexer_3_out0[0]);
  Selector selector_1 (
    ._00(demultiplexer_1_out0[0]), ._01(or_3_out), ._10(or_4_out), ._11(AluOutClk), .X_(InsRegSel),
    .out_6(RegSelClk));
  or or_5 (RegOutClk, demultiplexer_1_out0[1], demultiplexer_2_out0[1], demultiplexer_2_out0[4], demultiplexer_3_out0[1], demultiplexer_3_out2[1], MemClk);
  or or_6 (MemOutClk, demultiplexer_1_out0[2], demultiplexer_3_out0[1]);
  or or_7 (MemSelClk, demultiplexer_1_out0[2], demultiplexer_3_out0[1], demultiplexer_3_out2[1]);
  buf or_8 (CarryInClk, demultiplexer_1_out0[2]);  // OR_Gate
  Selector selector_2 (
    ._00(demultiplexer_3_out1[1]), ._01(demultiplexer_3_out0[3]), ._10(demultiplexer_2_out0[7]),
    ._11(demultiplexer_1_out0[2]), .X_(RegInpSel), .out_6(RegInClk));
  or or_9 (RegClk, demultiplexer_3_out1[2], demultiplexer_3_out0[4], demultiplexer_2_out0[8], demultiplexer_1_out0[3]);

  assign MemInClk = MemClk;

  // Notes on the sheet:
  //   CarryInClk: pull=down
  //   InsRegClk: pull=down
  //   Decode: pull=down
  //   RegInClk: pull=down
  //   RegOutClk: pull=down
  //   MemInClk: pull=down
  //   AluInAClk: pull=down
  //   RegClk: pull=down
  //   MemOutClk: pull=down
  //   N_Z_P_2: pull=down
  //   N_Z_P: pull=down
  //   RegSelClk: pull=down
  //   AluOutClk: pull=down
  //   MemSelClk: pull=down
  //   MemClk: pull=down
  //   AluInBClk: pull=down
endmodule

// 3
module _3_bit_register (
  input  Clock,
  input  [2:0] Input,
  input  Clock_2,
  output [2:0] Output
);

  D_Flip_Flop d_ff_1 (.clk(Clock), .D(Input[0]), .Q(Output[0]));  // open: Qn, preset, en, reset
  D_Flip_Flop d_ff_2 (.clk(Clock), .D(Input[1]), .Q(Output[1]));  // open: Qn, preset, en, reset
  D_Flip_Flop d_ff_3 (.clk(Clock), .D(Input[2]), .Q(Output[2]));  // open: Qn, preset, en, reset

  assign Clock_2 = Clock;
endmodule

// 5
module _5_bit_register (
  input  Clock,
  input  [4:0] Input,
  input  Clock_2,
  output [4:0] Output
);

  D_Flip_Flop d_ff_1 (.clk(Clock), .D(Input[0]), .Q(Output[0]));  // open: Qn, preset, en, reset
  D_Flip_Flop d_ff_2 (.clk(Clock), .D(Input[1]), .Q(Output[1]));  // open: Qn, preset, en, reset
  D_Flip_Flop d_ff_3 (.clk(Clock), .D(Input[2]), .Q(Output[2]));  // open: Qn, preset, en, reset
  D_Flip_Flop d_ff_4 (.clk(Clock), .D(Input[3]), .Q(Output[3]));  // open: Qn, preset, en, reset
  D_Flip_Flop d_ff_5 (.clk(Clock), .D(Input[4]), .Q(Output[4]));  // open: Qn, preset, en, reset

  assign Clock_2 = Clock;

  // Notes on the sheet:
  //   Input: pull=down
endmodule

// 8
module _8_bit_register (
  input  Clock,
  input  [7:0] Input,
  input  Clock_2,
  output [7:0] Output
);

  D_Flip_Flop d_ff_1 (.clk(Clock), .D(Input[0]), .Q(Output[0]));  // open: Qn, preset, en, reset
  D_Flip_Flop d_ff_2 (.clk(Clock), .D(Input[1]), .Q(Output[1]));  // open: Qn, preset, en, reset
  D_Flip_Flop d_ff_3 (.clk(Clock), .D(Input[2]), .Q(Output[2]));  // open: Qn, preset, en, reset
  D_Flip_Flop d_ff_4 (.clk(Clock), .D(Input[3]), .Q(Output[3]));  // open: Qn, preset, en, reset
  D_Flip_Flop d_ff_5 (.clk(Clock), .D(Input[4]), .Q(Output[4]));  // open: Qn, preset, en, reset
  D_Flip_Flop d_ff_6 (.clk(Clock), .D(Input[5]), .Q(Output[5]));  // open: Qn, preset, en, reset
  D_Flip_Flop d_ff_7 (.clk(Clock), .D(Input[6]), .Q(Output[6]));  // open: Qn, preset, en, reset
  D_Flip_Flop d_ff_8 (.clk(Clock), .D(Input[7]), .Q(Output[7]));  // open: Qn, preset, en, reset

  assign Clock_2 = Clock;
endmodule

// 16
module _16_bit_register (
  input  Clock,
  input  [15:0] Input,
  input  Clock_2,
  output [15:0] Output
);

  D_Flip_Flop d_ff_1 (.clk(Clock), .D(Input[14]), .Q(Output[14]));  // open: Qn, preset, en, reset
  D_Flip_Flop d_ff_2 (.clk(Clock), .D(Input[6]), .Q(Output[6]));  // open: Qn, preset, en, reset
  D_Flip_Flop d_ff_3 (.clk(Clock), .D(Input[8]), .Q(Output[8]));  // open: Qn, preset, en, reset
  D_Flip_Flop d_ff_4 (.clk(Clock), .D(Input[10]), .Q(Output[10]));  // open: Qn, preset, en, reset
  D_Flip_Flop d_ff_5 (.clk(Clock), .D(Input[12]), .Q(Output[12]));  // open: Qn, preset, en, reset
  D_Flip_Flop d_ff_6 (.clk(Clock), .D(Input[13]), .Q(Output[13]));  // open: Qn, preset, en, reset
  D_Flip_Flop d_ff_7 (.clk(Clock), .D(Input[15]), .Q(Output[15]));  // open: Qn, preset, en, reset
  D_Flip_Flop d_ff_8 (.clk(Clock), .D(Input[0]), .Q(Output[0]));  // open: Qn, preset, en, reset
  D_Flip_Flop d_ff_9 (.clk(Clock), .D(Input[2]), .Q(Output[2]));  // open: Qn, preset, en, reset
  D_Flip_Flop d_ff_10 (.clk(Clock), .D(Input[4]), .Q(Output[4]));  // open: Qn, preset, en, reset
  D_Flip_Flop d_ff_11 (.clk(Clock), .D(Input[5]), .Q(Output[5]));  // open: Qn, preset, en, reset
  D_Flip_Flop d_ff_12 (.clk(Clock), .D(Input[7]), .Q(Output[7]));  // open: Qn, preset, en, reset
  D_Flip_Flop d_ff_13 (.clk(Clock), .D(Input[9]), .Q(Output[9]));  // open: Qn, preset, en, reset
  D_Flip_Flop d_ff_14 (.clk(Clock), .D(Input[11]), .Q(Output[11]));  // open: Qn, preset, en, reset
  D_Flip_Flop d_ff_15 (.clk(Clock), .D(Input[1]), .Q(Output[1]));  // open: Qn, preset, en, reset
  D_Flip_Flop d_ff_16 (.clk(Clock), .D(Input[3]), .Q(Output[3]));  // open: Qn, preset, en, reset

  assign Clock_2 = Clock;
endmodule

module Instruction_Register (
  input  Decode,
  input  [15:0] In,
  input  Clock,
  output [15:0] Out
);

  Register #(.width(16), .trigger("high")) register_1 (.D(In), .clk(Clock));  // open: en, Q, clr

  assign Out = 16'h994c;
endmodule

module Carry_In (
  input  Carry_In,
  input  [15:0] IN,
  output [15:0] Out
);

  Adder #(.width(16)) adder_1 (.a(IN), .b({16{1'b0}}), .out(Out), .cin(Carry_In));  // open: cout

  // Notes on the sheet:
  //   Out: pull=down
endmodule

module Memory (
  input  CLEAR,
  input  [15:0] Memory_Address,
  input  [15:0] Data_In,
  input  Clock,
  output [15:0] Data_Out
);

  RAM #(.addrWidth(16), .dataWidth(16), .bus("separate")) ram_1 (
    .addr(Memory_Address), .din(Data_In), .data(Data_Out), .str(1'b1), .sel(1'b1), .clk(Clock), .ld(1'b1),
    .clr(CLEAR));

  // Notes on the sheet:
  //   Data_Out: pull=down
endmodule

module AddTwoNum (
  input  CLEAR,
  input  [15:0] Memory_Address,
  input  [15:0] Data_In,
  input  Clock,
  output [15:0] Data_Out
);

  Multiplexer #(.select(4), .width(16), .enable("false")) multiplexer_1 (
    .in0(16'h90f), .in1(16'haf0), .in2(16'h994c), .in3(16'hc04), .in4(16'hb80), .in5(16'h6000),
    .out(Data_Out), .sel(Memory_Address[3:0]));  // open: in6, in7, in8, in9, in10, in11, in12, in13, in14, in15

  // Notes on the sheet:
  //   Data_Out: pull=down
endmodule

module Selector (
  input  _00,
  input  _01,
  input  _10,
  input  _11,
  output [1:0] X_,
  output out_6
);

  or or_1 (X_[1], _11, _10);
  or or_2 (X_[0], _11, _01);
  or or_3 (out_6, _11, _10, _01, _00);

  // Notes on the sheet:
  //   _00: pull=down
  //   _01: pull=down
  //   _11: pull=down
  //   _10: pull=down
endmodule

module Counter (
);

  wire clock_1_out, clock_2_out, flipflo_1_out_1, flipflo_1_out_2, flipflo_2_out_2, flipflo_3_out_1,
       flipflo_3_out_2, nand_1_out, nand_2_out, nand_3_out, nand_4_out, nand_5_out, nand_6_out, nand_7_out,
       nand_8_out, nand_9_out, nand_10_out, nand_11_out, nand_12_out, nand_13_out, nand_14_out, nand_15_out;

  Clock clock_1 (.out(clock_1_out));
  Clock clock_2 (.out(clock_2_out));
  LED led_1 (.in(flipflo_1_out_2));
  FlipFlo flipflo_1 (.in_1(flipflo_1_out_2), .sync(clock_1_out), .out_1(flipflo_1_out_1), .out_2(flipflo_1_out_2));
  LED led_2 (.in(flipflo_3_out_2));
  FlipFlo flipflo_2 (.in_1(flipflo_2_out_2), .sync(flipflo_3_out_1), .out_2(flipflo_2_out_2));  // open: out_1
  FlipFlo flipflo_3 (.in_1(flipflo_3_out_2), .sync(flipflo_1_out_1), .out_1(flipflo_3_out_1), .out_2(flipflo_3_out_2));
  nand nand_1 (nand_1_out, nand_5_out, clock_2_out);
  nand nand_2 (nand_2_out, clock_2_out, nand_3_out);
  nand nand_3 (nand_3_out, nand_5_out, nand_5_out);
  LED led_3 (.in(flipflo_2_out_2));
  nand nand_4 (nand_4_out, nand_1_out, nand_5_out);
  nand nand_5 (nand_5_out, nand_4_out, nand_2_out);
  nand nand_6 (nand_6_out, nand_10_out, nand_4_out);
  nand nand_7 (nand_7_out, nand_4_out, nand_8_out);
  nand nand_8 (nand_8_out, nand_10_out, nand_10_out);
  nand nand_9 (nand_9_out, nand_6_out, nand_10_out);
  nand nand_10 (nand_10_out, nand_9_out, nand_7_out);
  nand nand_11 (nand_11_out, nand_15_out, nand_15_out);
  nand nand_12 (nand_12_out, nand_15_out, nand_9_out);
  nand nand_13 (nand_13_out, nand_9_out, nand_11_out);
  nand nand_14 (nand_14_out, nand_12_out, nand_15_out);
  nand nand_15 (nand_15_out, nand_14_out, nand_13_out);
endmodule

module FlipFlo (
  input  in_1,
  input  sync,
  output out_1,
  output out_2
);

  wire nand_1_out, nand_2_out, nand_3_out;

  nand nand_1 (nand_1_out, in_1, sync);
  nand nand_2 (nand_2_out, sync, nand_3_out);
  nand nand_3 (nand_3_out, in_1, in_1);
  nand nand_4 (out_1, nand_1_out, out_2);
  nand nand_5 (out_2, out_1, nand_2_out);
endmodule

module Decider (
  input  N1,
  input  N2,
  input  Z1,
  input  Z2,
  input  P1,
  input  P2,
  input  Clock,
  output Reset
);

  wire and_1_out, and_2_out, and_3_out, or_1_out;

  and and_1 (and_1_out, N1, N2);
  or or_1 (or_1_out, and_1_out, and_2_out, and_3_out);
  and and_2 (and_2_out, Z1, Z2);
  and and_3 (and_3_out, P1, P2);
  and and_4 (Reset, or_1_out, Clock);
endmodule
